# Fritzing sketch Schaltplan (saved by Fritzing 0.9.3b)
breadboards: 1

parts:
  Bauteil1 = Arduino Uno (Rev3)
  LED1 = LED - 3mm [color="Red (633nm)" package="3 mm [THT]"]
  MIC1 = Adafruit TSL2561 Digital Luminosity/Lux/Light Sensor
  R1 = Resistor [tolerance=±5% resistance=220 package="1206 [SMD]"]

nets:
  N1: Bauteil1.A4/SDA, MIC1.SDA
  N2: Bauteil1.A5/SCL, MIC1.SCL
  GND: Bauteil1.GND, MIC1.GND, R1.Pin_1
  N3: Bauteil1.D5_PWM, LED1.anode
  5V: Bauteil1.5V, MIC1.VIN
  N4: LED1.cathode, R1.Pin_0
